// Logisim project alu.circ as structural Verilog: 1 circuit, main circuit alu
module alu (
  input  [31:0] A,
  input  [31:0] in_2,
  input  [31:0] B,
  input  [31:0] in_4,
  input  [3:0] ALUSel,
  output [31:0] Result
);

  wire comparator_1_lt;
  wire [4:0] bit_extender_1_out, bit_extender_2_out, bit_extender_3_out, bit_extender_4_out;
  wire [31:0] add0, add1, divu8, mul10, mulh14, mulhu11, multiplier_2_cout, multiplier_3_cout,
       multiplier_4_cout, negator_1_out, negator_2_out, negator_3_out, negator_4_out, not_1_out, not_2_out,
       or2, remu9, sll6, slt7, sra5, srl4, sub12, xor3;

  Multiplexer #(.select(4), .width(32), .enable("false")) multiplexer_1 (
    .in0(add0), .in1(add1), .in2(or2), .in3(xor3), .in4(srl4), .in5(sra5), .in6(sll6), .in7(slt7),
    .in8(divu8), .in9(remu9), .in10(mul10), .in11(mulhu11), .in12(sub12), .in13(B), .in14(mulh14),
    .out(Result), .sel(ALUSel));  // open: in15
  Bit_Extender #(.in_width(32), .out_width(5)) bit_extender_1 (.in(B), .out(bit_extender_1_out));
  Bit_Extender #(.in_width(32), .out_width(5)) bit_extender_2 (.in(B), .out(bit_extender_2_out));
  Bit_Extender #(.in_width(32), .out_width(5)) bit_extender_3 (.in(B), .out(bit_extender_3_out));
  Adder #(.width(32)) adder_1 (.a(A), .b(B), .out(add0));  // open: cin, cout
  assign add1 = A & B;  // AND_Gate and_1, 32 bits wide
  assign or2 = A | B;  // OR_Gate or_1, 32 bits wide
  assign xor3 = A ^ B;  // XOR_Gate xor_1, 32 bits wide
  Shifter #(.width(32), .shift("lr")) shifter_1 (.in(A), .\dist (bit_extender_1_out), .out(srl4));
  Shifter #(.width(32), .shift("ar")) shifter_2 (.in(A), .\dist (bit_extender_2_out), .out(sra5));
  Shifter #(.width(32)) shifter_3 (.in(A), .\dist (bit_extender_3_out), .out(sll6));
  Shifter #(.width(32)) shifter_4 (.in(A), .\dist (bit_extender_4_out), .out(sll6));
  Bit_Extender #(.in_width(32), .out_width(5)) bit_extender_4 (.in(B), .out(bit_extender_4_out));
  Comparator #(.width(32)) comparator_1 (.a(A), .b(B), .lt(comparator_1_lt));  // open: gt, eq
  assign slt7 = {{31{1'b0}}, comparator_1_lt};  // Bit_Extender bit_extender_5
  Divider #(.width(32)) divider_1 (.a(A), .b(B), .out(divu8), .rem(remu9));  // open: upper
  Multiplier #(.width(32)) multiplier_1 (.a(A), .b(B), .out(mul10), .cout(mulhu11));  // open: cin
  Negator #(.width(32)) negator_1 (.in(A), .out(negator_1_out));
  Multiplier #(.width(32)) multiplier_2 (.a(negator_1_out), .b(B), .cout(multiplier_2_cout));  // open: out, cin
  Negator #(.width(32)) negator_2 (.in(B), .out(negator_2_out));
  Multiplier #(.width(32)) multiplier_3 (.a(negator_2_out), .b(A), .cout(multiplier_3_cout));  // open: out, cin
  Negator #(.width(32)) negator_3 (.in(B), .out(negator_3_out));
  Multiplier #(.width(32)) multiplier_4 (
    .a(negator_3_out), .b(negator_4_out), .cout(multiplier_4_cout));  // open: out, cin
  Negator #(.width(32)) negator_4 (.in(A), .out(negator_4_out));
  assign not_1_out = ~multiplier_2_cout;  // NOT_Gate not_1, 32 bits wide
  assign not_2_out = ~multiplier_3_cout;  // NOT_Gate not_2, 32 bits wide
  Multiplexer #(.select(2), .width(32), .enable("false")) multiplexer_2 (
    .in0(mulhu11), .in1(not_1_out), .in2(not_2_out), .in3(multiplier_4_cout), .out(mulh14),
    .sel({B[31], A[31]}));
  Subtractor #(.width(32)) subtractor_1 (.a(A), .b(B), .out(sub12));  // open: bin, bout

  // Other names for the same wires on the sheet: bsel13[31:0] = B

  // Notes on the sheet:
  //   INPUTS to your circuit
  //   DON'T CHANGE THE LOCATIONS OF THE INPUTS AND OUTPUTS!
  //   OUTPUT from your circuit
endmodule
