// Logisim project control_logic.circ as structural Verilog: 1 circuit, main circuit control_logic
module control_logic (
  input  [31:0] inst,
  input  BrEq,
  input  BrLt,
  output PCSel,
  output RegWEn,
  output [2:0] ImmSel,
  output BrUn,
  output ASel,
  output BSel,
  output [3:0] ALUSel,
  output MemRW,
  output [1:0] WBSel
);

  wire and_1_out, and_2_out, and_5_out, and_6_out, and_7_out, and_8_out, and_9_out, and_10_out, and_11_out,
       and_12_out, and_13_out, and_14_out, and_15_out, and_16_out, and_23_out, and_24_out, and_25_out,
       and_26_out, and_27_out, and_28_out, and_29_out, and_30_out, and_31_out, and_33_out, and_34_out,
       and_35_out, is_add0, is_add1, is_divu8, is_func3_0, is_func3_1, is_func3_2, is_func3_3, is_func3_4,
       is_func3_5, is_func3_6, is_func3_7, is_func7_0, is_func7_1, is_func7_20, is_I3_Load, is_I13_Arith,
       is_I67_Jalr, is_I_imm5, is_mul_10, is_mulh14, is_mulhu11, is_or2, is_R, is_remu9, is_SB, is_sll6,
       is_slt7, is_sra5, is_srl4, is_sub12, is_U_17, is_U_37, is_UJ, is_xor3, not_2_out, not_3_out, or_6_out,
       or_7_out, or_10_out;
  wire [4:1] is_I_out;

  and and_1 (and_1_out, and_5_out, is_func7_0);
  or or_1 (is_add0, and_1_out, and_2_out);
  and and_2 (and_2_out, is_I13_Arith, is_func3_0);
  or or_2 (is_add1, and_7_out, and_8_out);
  or or_3 (is_or2, and_10_out, and_11_out);
  or or_4 (is_xor3, and_13_out, and_14_out);
  and and_3 (is_srl4, and_15_out, or_6_out);
  and and_4 (is_sra5, and_16_out, or_7_out);
  Comparator #(.width(7)) comparator_1 (.a(inst[6:0]), .b(7'b0110011), .eq(is_R));  // open: gt, lt
  Comparator #(.width(7)) comparator_2 (.a(inst[6:0]), .b(7'b0010011), .eq(is_I13_Arith));  // open: gt, lt
  Comparator #(.width(7)) comparator_3 (.a(inst[6:0]), .b(7'b0100011), .eq(MemRW));  // open: gt, lt
  Comparator #(.width(7)) comparator_4 (.a(inst[6:0]), .b(7'b1100011), .eq(is_SB));  // open: gt, lt
  Comparator #(.width(7)) comparator_5 (.a(inst[6:0]), .b(7'b0010111), .eq(is_U_17));  // open: gt, lt
  Comparator #(.width(7)) comparator_6 (.a(inst[6:0]), .b(7'b0110111), .eq(is_U_37));  // open: gt, lt
  Comparator #(.width(7)) comparator_7 (.a(inst[6:0]), .b(7'b1101111), .eq(is_UJ));  // open: gt, lt
  Comparator #(.width(7)) comparator_8 (.a(inst[6:0]), .b(7'b0000011), .eq(is_I3_Load));  // open: gt, lt
  Comparator #(.width(7)) comparator_9 (.a(inst[6:0]), .b(7'b1100111), .eq(is_I67_Jalr));  // open: gt, lt
  or or_5 (is_I_imm5, is_I13_Arith, is_func3_5);
  and and_5 (and_5_out, is_R, is_func3_0);
  and and_6 (and_6_out, is_R, is_func3_7);
  and and_7 (and_7_out, and_6_out, is_func7_0);
  and and_8 (and_8_out, is_I13_Arith, is_func3_7);
  and and_9 (and_9_out, is_R, is_func3_6);
  and and_10 (and_10_out, and_9_out, is_func7_0);
  and and_11 (and_11_out, is_I13_Arith, is_func3_6);
  and and_12 (and_12_out, is_R, is_func3_4);
  and and_13 (and_13_out, and_12_out, is_func7_0);
  and and_14 (and_14_out, is_I13_Arith, is_func3_4);
  and and_15 (and_15_out, is_func3_5, is_func7_0);
  or or_6 (or_6_out, is_R, is_I13_Arith);
  and and_16 (and_16_out, is_func3_5, is_func7_20);
  or or_7 (or_7_out, is_R, is_I13_Arith);
  and and_17 (is_divu8, and_25_out, is_func7_1);
  and and_18 (is_remu9, and_26_out, is_func7_1);
  and and_19 (is_mul_10, and_27_out, is_func7_1);
  and and_20 (is_mulhu11, and_28_out, is_func7_1);
  and and_21 (is_sub12, and_29_out, is_func7_20);
  and and_22 (is_mulh14, and_30_out, is_func7_1);
  and and_23 (and_23_out, and_31_out, is_func7_0);
  or or_8 (is_sll6, and_23_out, and_24_out);
  and and_24 (and_24_out, is_I13_Arith, is_func3_1);
  BitFinder #(.width(3)) bitfinder_1 (.in({is_I3_Load, is_R, 1'b0}), .index(WBSel));  // open: found
  not not_1 (BSel, is_R);
  and and_25 (and_25_out, is_R, is_func3_5);
  and and_26 (and_26_out, is_R, is_func3_7);
  and and_27 (and_27_out, is_R, is_func3_0);
  and and_28 (and_28_out, is_R, is_func3_3);
  and and_29 (and_29_out, is_R, is_func3_0);
  and and_30 (and_30_out, is_R, is_func3_1);
  and and_31 (and_31_out, is_R, is_func3_1);
  Comparator #(.width(3)) comparator_10 (.a(inst[14:12]), .b(3'b000), .eq(is_func3_0));  // open: gt, lt
  Comparator #(.width(3)) comparator_11 (.a(inst[14:12]), .b(3'b001), .eq(is_func3_1));  // open: gt, lt
  Comparator #(.width(3)) comparator_12 (.a(inst[14:12]), .b(3'b010), .eq(is_func3_2));  // open: gt, lt
  Comparator #(.width(3)) comparator_13 (.a(inst[14:12]), .b(3'b011), .eq(is_func3_3));  // open: gt, lt
  Comparator #(.width(3)) comparator_14 (.a(inst[14:12]), .b(3'b100), .eq(is_func3_4));  // open: gt, lt
  Comparator #(.width(3)) comparator_15 (.a(inst[14:12]), .b(3'b101), .eq(is_func3_5));  // open: gt, lt
  Comparator #(.width(3)) comparator_16 (.a(inst[14:12]), .b(3'b110), .eq(is_func3_6));  // open: gt, lt
  Comparator #(.width(3)) comparator_17 (.a(inst[14:12]), .b(3'b111), .eq(is_func3_7));  // open: gt, lt
  Comparator #(.width(7)) comparator_18 (.a(inst[31:25]), .b({7{1'b0}}), .eq(is_func7_0));  // open: gt, lt
  Comparator #(.width(7)) comparator_19 (.a(inst[31:25]), .b(7'b0000001), .eq(is_func7_1));  // open: gt, lt
  Comparator #(.width(7)) comparator_20 (.a(inst[31:25]), .b(7'b0100000), .eq(is_func7_20));  // open: gt, lt
  not not_2 (not_2_out, MemRW);
  not not_3 (not_3_out, is_SB);
  and and_32 (RegWEn, not_2_out, not_3_out);
  or or_9 (is_slt7, and_34_out, and_35_out);
  and and_33 (and_33_out, is_R, is_func3_2);
  and and_34 (and_34_out, and_33_out, is_func7_0);
  and and_35 (and_35_out, is_I13_Arith, is_func3_2);
  or or_10 (or_10_out, is_I13_Arith, is_I3_Load);
  BitFinder #(.width(15)) bitfinder_2 (
    .in({is_mulh14, 1'b0, is_sub12, is_mulhu11, is_mul_10, is_remu9, is_divu8, is_slt7, is_sll6, is_sra5, is_srl4, is_xor3, is_or2, is_add1, is_add0}),
    .index(ALUSel));  // open: found
  or is_I (is_I_out[1], or_10_out, is_I67_Jalr);
  or or_11 (is_I_out[4], is_U_17, is_U_37);
  BitFinder #(.width(6)) bitfinder_3 (
    .in({is_UJ, is_I_out[4], is_SB, MemRW, is_I_out[1], is_I_imm5}), .index(ImmSel));  // open: found

  // Other names for the same wires on the sheet: is_S = MemRW; i_0_6_op[6:0] = inst[6:0]; i_7_11_rd[4:0] = inst[11:7];
  //   i_12_14_func3[2:0] = inst[14:12]; i_15_19_rs1[4:0] = inst[19:15]; i_20_24_rs2[4:0] = inst[24:20];
  //   i_25_31_func7[6:0] = inst[31:25]

  // Notes on the sheet:
  //   INPUTS to your circuit
  //   DON'T CHANGE THE LOCATIONS OF THE INPUTS AND OUTPUTS!
  //   OUTPUT from your circuit
endmodule
