// Logisim project cpu.circ as structural Verilog: 1 circuit, main circuit main
module main (
  input  [31:0] INSTRUCTION,
  input  CLOCK,
  output [31:0] PROGRAM_COUNTER,
  output [31:0] ra,
  output [31:0] sp,
  output [31:0] t0,
  output [31:0] t1,
  output [31:0] t2,
  output [31:0] s0,
  output [31:0] s1,
  output [31:0] a0
);

  wire control_logic_1_bsel, control_logic_1_memrw, control_logic_1_regwen, undriven;
  wire [1:0] bit_extender_5_out, control_logic_1_wbsel;
  wire [2:0] control_logic_1_immsel, i_12_14_func3;
  wire [3:0] control_logic_1_alusel;
  wire [4:0] i_7_11_rd, i_15_19_rs1, i_20_24_rs2;
  wire [6:0] i_0_6_op, i_25_31_func7;
  wire [7:0] bit_extender_1_out;
  wire [15:0] bit_extender_3_out;
  wire [31:0] adder_1_out, Arithmetic_Logic_Unit_result, bit_extender_2_out, bit_extender_4_out, DMEM_p5,
       imm_out, multiplexer_1_out, multiplexer_2_out, multiplexer_3_out, out_rs2, RegFile_read_data_1;

  control_logic control_logic_1 (
    .BSel(control_logic_1_bsel), .RegWEn(control_logic_1_regwen), .ImmSel(control_logic_1_immsel),
    .ALUSel(control_logic_1_alusel), .MemRW(control_logic_1_memrw), .WBSel(control_logic_1_wbsel));  // open: BrUn, ASel, PCSel, BrLt, BrEq, inst
  Adder #(.width(32)) adder_1 (.a(PROGRAM_COUNTER), .b(32'h4), .out(adder_1_out));  // open: cin, cout
  Register #(.width(32)) PC (.D(adder_1_out), .clk(CLOCK), .Q(PROGRAM_COUNTER));  // open: en, clr
  imm_gen imm_gen_1 (
    .ImmSel(control_logic_1_immsel),
    .inst({i_25_31_func7, i_20_24_rs2, i_15_19_rs1, i_12_14_func3, i_7_11_rd, i_0_6_op}), .imm(imm_out));
  Register #(.width(32)) register_1 (
    .D(INSTRUCTION), .clk(CLOCK),
    .Q({i_25_31_func7, i_20_24_rs2, i_15_19_rs1, i_12_14_func3, i_7_11_rd, i_0_6_op}), .clr(undriven));  // open: en
  regfile_main RegFile (
    .rs2(i_20_24_rs2), .rd(i_7_11_rd), .Read_Data_1(RegFile_read_data_1), .Read_Data_2(out_rs2), .ra(ra),
    .sp(sp), .t0(t0), .t1(t1), .t2(t2), .s0(s0), .s1(s1), .a0(a0), .rs1(i_15_19_rs1),
    .Write_Data(multiplexer_3_out), .RegWEn(control_logic_1_regwen), .clk(CLOCK));  // open: in_7
  // branch_comp branch_comp_1: pin names not known
  Multiplexer #(.width(32), .enable("false")) multiplexer_1 (
    .in0(out_rs2), .in1(imm_out), .out(multiplexer_1_out), .sel(control_logic_1_bsel));
  alu Arithmetic_Logic_Unit (
    .Result(Arithmetic_Logic_Unit_result), .ALUSel(control_logic_1_alusel), .A(RegFile_read_data_1),
    .B(multiplexer_1_out));  // open: in_2, in_4
  Bit_Extender #(.in_width(32), .out_width(8)) bit_extender_1 (.in(DMEM_p5), .out(bit_extender_1_out));
  assign bit_extender_2_out = {{24{bit_extender_1_out[7]}}, bit_extender_1_out};  // Bit_Extender bit_extender_2
  Bit_Extender #(.in_width(32)) bit_extender_3 (.in(DMEM_p5), .out(bit_extender_3_out));
  assign bit_extender_4_out = {{16{bit_extender_3_out[15]}}, bit_extender_3_out};  // Bit_Extender bit_extender_4
  // mem_main DMEM: pin names not known; wires that end beside it: Arithmetic_Logic_Unit_result, out_rs2, CLOCK, control_logic_1_memrw, DMEM_p5
  Multiplexer #(.select(2), .width(32), .enable("false")) multiplexer_2 (
    .in0(bit_extender_2_out), .in1(bit_extender_4_out), .in2(DMEM_p5), .out(multiplexer_2_out),
    .sel(bit_extender_5_out));  // open: in3
  Bit_Extender #(.in_width(3), .out_width(2)) bit_extender_5 (.in(i_12_14_func3), .out(bit_extender_5_out));
  Multiplexer #(.select(2), .width(32), .enable("false")) multiplexer_3 (
    .in1(Arithmetic_Logic_Unit_result), .in2(multiplexer_2_out), .out(multiplexer_3_out),
    .sel(control_logic_1_wbsel));  // open: in0, in3

  // Other names for the same wires on the sheet: clk = CLOCK;
  //   ins_d[31:0] = {i_25_31_func7, i_20_24_rs2, i_15_19_rs1, i_12_14_func3, i_7_11_rd, i_0_6_op}

  // Notes on the sheet:
  //   Output
  //   IMEM (do **NOT** move this)
  //   Inputs
  //   Inputs/Outputs for testing. Do **NOT** move these.
endmodule
