// Logisim project imm_gen.circ as structural Verilog: 1 circuit, main circuit imm_gen
module imm_gen (
  input  [31:0] inst,
  input  [2:0] ImmSel,
  output [31:0] imm
);

  wire is_I3_Load, is_I13_Arith, is_I67_Jalr, is_S, is_SB, is_U_17, is_U_37, is_UJ;
  wire [31:0] bit_extender_1_out, bit_extender_2_out, bit_extender_3_out, bit_extender_4_out,
       bit_extender_5_out, bit_extender_6_out;

  Comparator #(.width(7)) comparator_1 (.a(inst[6:0]), .b(7'b0010011), .eq(is_I13_Arith));  // open: gt, lt
  Comparator #(.width(7)) comparator_2 (.a(inst[6:0]), .b(7'b0100011), .eq(is_S));  // open: gt, lt
  Comparator #(.width(7)) comparator_3 (.a(inst[6:0]), .b(7'b1100011), .eq(is_SB));  // open: gt, lt
  Comparator #(.width(7)) comparator_4 (.a(inst[6:0]), .b(7'b0010111), .eq(is_U_17));  // open: gt, lt
  Comparator #(.width(7)) comparator_5 (.a(inst[6:0]), .b(7'b0110111), .eq(is_U_37));  // open: gt, lt
  Comparator #(.width(7)) comparator_6 (.a(inst[6:0]), .b(7'b1101111), .eq(is_UJ));  // open: gt, lt
  Comparator #(.width(7)) comparator_7 (.a(inst[6:0]), .b(7'b0000011), .eq(is_I3_Load));  // open: gt, lt
  Comparator #(.width(7)) comparator_8 (.a(inst[6:0]), .b(7'b1100111), .eq(is_I67_Jalr));  // open: gt, lt
  assign bit_extender_1_out = {{27{inst[24]}}, inst[24:20]};  // Bit_Extender bit_extender_1
  assign bit_extender_2_out = {{20{inst[31]}}, inst[31:20]};  // Bit_Extender bit_extender_2
  assign bit_extender_3_out = {{20{inst[31]}}, {inst[31:25], inst[11:7]}};  // Bit_Extender bit_extender_3
  assign bit_extender_4_out = {{19{inst[31]}}, {inst[31], inst[7], inst[30:25], inst[11:8], 1'b0}};  // Bit_Extender bit_extender_4
  assign bit_extender_5_out = {{12{inst[31]}}, inst[31:12]};  // Bit_Extender bit_extender_5
  assign bit_extender_6_out = {{11{inst[31]}}, {inst[31], inst[19:12], inst[20], inst[30:21], 1'b0}};  // Bit_Extender bit_extender_6
  Multiplexer #(.select(3), .width(32), .enable("false")) multiplexer_1 (
    .in0(bit_extender_1_out), .in1(bit_extender_2_out), .in2(bit_extender_3_out), .in3(bit_extender_4_out),
    .in4(bit_extender_5_out), .in5(bit_extender_6_out), .out(imm), .sel(ImmSel));  // open: in6, in7

  // Other names for the same wires on the sheet: i_7_11_rd[4:0] = inst[11:7]; i_8_11[3:0] = inst[11:8]; i_7 = inst[7];
  //   i_20_24_rs2[4:0] = inst[24:20]; i_21_24[3:0] = inst[24:21]; i_25_30[5:0] = inst[30:25];
  //   i_25_31_func7[6:0] = inst[31:25]; i_20 = inst[20]; i_12_14_func3[2:0] = inst[14:12];
  //   i_15_19_rs1[4:0] = inst[19:15]; i_31 = inst[31]; i_0_6_op[6:0] = inst[6:0]

  // Notes on the sheet:
  //   INPUTS to your circuit
  //   DON'T CHANGE THE LOCATIONS OF THE INPUTS AND OUTPUTS!
  //   OUTPUT from your circuit
endmodule
